// Digital circuit fetcher.dig as structural Verilog
module fetcher (
  input  [31:0] Addr,
  input  C,
  input  Pwr,
  input  [7:0] D,
  output [31:0] Val,
  output Done,
  output [23:0] A,
  output OE
);

  wire and_1_out, and_2_out, delay_1_out, delay_2_out, delay_4_out, delay_6_out, demultiplexer_1_out_0,
       demultiplexer_1_out_1, demultiplexer_1_out_2, demultiplexer_1_out_3, not_1_out, or_1_out, or_2_out;
  wire [1:0] INST_SIZE_COUNTER_out;
  wire [7:0] delay_5_out;

  or or_1 (or_1_out, and_1_out, C);
  or or_2 (or_2_out, and_1_out, C);
  Delay delay_1 (.in(C), .out(delay_1_out));
  Counter #(.Bits(2)) INST_SIZE_COUNTER (
    .en(Pwr), .C(or_1_out), .clr(delay_1_out), .out(INST_SIZE_COUNTER_out));  // open: ovf
  Delay delay_2 (.in(or_2_out), .out(delay_2_out));
  Add #(.Bits(24)) add_1 (.a({{22{1'b0}}, INST_SIZE_COUNTER_out}), .b(Addr[23:0]), .c_i(1'b0), .s(A));  // open: c_o
  Delay delay_3 (.in(delay_2_out), .out(OE));
  and and_1 (and_1_out, delay_4_out, not_1_out);
  Delay delay_4 (.in(OE), .out(delay_4_out));
  and and_2 (and_2_out, INST_SIZE_COUNTER_out[0], INST_SIZE_COUNTER_out[1]);
  Delay #(.Bits(8)) delay_5 (.in(D), .out(delay_5_out));
  Demultiplexer #(.Selector_Bits(2)) demultiplexer_1 (
    .sel(INST_SIZE_COUNTER_out), .in(delay_4_out), .out_0(demultiplexer_1_out_0),
    .out_1(demultiplexer_1_out_1), .out_2(demultiplexer_1_out_2), .out_3(demultiplexer_1_out_3));
  not not_1 (not_1_out, and_2_out);
  Delay #(.delayTime(2)) delay_6 (.in(and_2_out), .out(delay_6_out));
  Register #(.Bits(8)) i0 (.D(delay_5_out), .C(demultiplexer_1_out_0), .en(Pwr), .Q(Val[7:0]));
  Register #(.Bits(8)) i1 (.D(delay_5_out), .C(demultiplexer_1_out_1), .en(Pwr), .Q(Val[15:8]));
  Register #(.Bits(8)) i2 (.D(delay_5_out), .C(demultiplexer_1_out_2), .en(Pwr), .Q(Val[23:16]));
  Register #(.Bits(8)) i3 (.D(delay_5_out), .C(demultiplexer_1_out_3), .en(Pwr), .Q(Val[31:24]));
  pulse #(.generic("Duration := 1;")) pulse_1 (.In(delay_6_out), .Out(Done));

  // Notes on the sheet:
  //   ROM
endmodule
